# Fritzing sketch DiagramaDeConexiones (saved by Fritzing 0.9.3b)
breadboards: 2

parts:
  U1 = ESP32-38PinWide [part_number=ESP32-38PinWide]
  JP1 = Header 3 [package=screwterminal-3.5mm-3_lock.007s]
  R1 = Resistor [tolerance=±5% resistance=1k package="2010 [SMD]"]
  R2 = Resistor [tolerance=±5% resistance=330 package="2010 [SMD]"]
  R3 = Resistor [tolerance=±5% resistance=330 package="2010 [SMD]"]
  R4 = Resistor [tolerance=±5% resistance=1k package="2010 [SMD]"]
  LED1 = LED - 5mm [color="Red (633nm)" package="5 mm [THT]"]
  Q1 = NPN-Transistor [package="TO92 [THT]"]
  Q2 = NPN-Transistor [package="TO92 [THT]"]
  JACK1 = 2.1mm Barrel Jack with Terminal Block  # not connected
  JACK2 = 2.1mm Barrel Jack with Terminal Block  # not connected
  M1 = MT3608 Module
  JACK3 = 2.1mm Barrel Jack with Terminal Block

nets:
  N1: U1.3.3, R1.Pin_0, R3.Pin_1, R4.Pin_1, Q2.C
  N2: U1.GPIO32, R1.Pin_1, R2.Pin_0
  N3: U1.GPIO33, LED1.anode
  N4: U1.GPIO25, JP1.1
  N5: U1.GPIO26, JP1.2
  N6: U1.GPIO27, JP1.3
  N7: U1.VIN, Q1.E, M1.pin2
  N8: R3.Pin_0, LED1.cathode
  N9: R4.Pin_0, Q1.B
  N10: Q1.C, Q2.B
  N11: Q2.E, M1.pin1
  N12: M1.pin3, JACK3.POS
  N13: M1.pin4, JACK3.NEG

notes:
  Sensores
  Elevador
  Micro
  Actuadores
  By: EVRV

custom parts:
  ESP32-38PinWide: Generic 38-Pin ESP32 with wide format (only access to one side of pins on a breadboard) based on Stephen Lilley's HiLetgo ESP-WROOM-32 ESP32 ESP-32S Development Board.
  MT3608 Module: MT3608 Boost Converter Module Links: Aerosemi MT3608 2A Step Up Converter datasheet
